// Logisim project roustel.circ as structural Verilog: 1 circuit, main circuit main
module main (
);

  wire adder_1_cout, adder_3_cout, adder_4_cout, and_1_out, and_2_out, and_3_out, and_4_out, and_5_out,
       and_6_out, and_7_out, and_8_out, and_9_out, and_10_out, and_11_out, and_13_out, and_14_out,
       and_15_out, and_16_out, and_17_out, C_q, clock_1_out, clock_2_out, comparator_1_eq, comparator_2_eq,
       comparator_3_gt, comparator_4_eq, comparator_5_gt, comparator_6_eq, comparator_6_lt, decoder_1_out0,
       decoder_1_out1, decoder_1_out2, decoder_1_out3, decoder_1_out4, decoder_1_out5, decoder_1_out6,
       decoder_1_out7, decoder_2_out0, decoder_2_out1, decoder_2_out2, decoder_2_out3, decoder_2_out4,
       decoder_2_out5, decoder_2_out6, decoder_2_out7, decoder_2_out8, decoder_2_out9, decoder_2_out10,
       decoder_2_out11, decoder_2_out12, decoder_2_out13, decoder_2_out14, decoder_2_out15, decoder_2_out16,
       decoder_2_out17, decoder_2_out18, decoder_2_out19, decoder_2_out20, decoder_2_out21, decoder_2_out22,
       decoder_2_out23, decoder_2_out24, decoder_2_out25, decoder_2_out26, decoder_2_out27, decoder_2_out28,
       decoder_2_out29, decoder_2_out30, decoder_2_out31, FF1_qn, FF2_q, FF2_qn, FF3_qn, FF4_q, FF4_qn,
       FF5_q, FF5_qn, FF6_q, FF6_qn, FF7_q, FF7_qn, FF8_q, FF8_qn, FF9_q, FF9_qn, FF10_q, FF10_qn,
       light_flash_q, multiplexer_10_out, N_q, nor_1_out, nor_2_out, not_1_out, not_2_out, not_3_out,
       not_4_out, not_5_out, not_6_out, not_7_out, not_8_out, not_9_out, not_10_out, or_1_out, or_2_out,
       or_3_out, or_4_out, or_5_out, or_6_out, or_7_out, or_8_out, or_10_out, subtractor_1_bout,
       subtractor_2_bout, Z_q;
  wire [2:0] multiplexer_1_out, multiplexer_3_out;
  wire [4:0] multiplexer_3_out_2;
  wire [7:0] adder_3_out, adder_4_out, and_12_out, ar_q, bit_extender_1_out, br_q, controlled_buffer_1_out,
       cr_q, FR1_q, FR2_q, FR3_q, FR4_q, FR5_q, FR6_q, FR7_q, FR8_q, ir_q, jr_q, multiplexer_4_out,
       multiplexer_6_out, multiplexer_7_out, multiplexer_8_out, multiplexer_9_out, multiplexer_11_out,
       multiplexer_13_out, negator_1_out, not_11_out, or_9_out, shifter_1_out, shifter_2_out, sr_q,
       subtractor_1_out, subtractor_2_out, ur_q, xor_1_out;
  wire [15:0] adder_1_out, bit_extender_2_out, counter_1_q, FR9_q, multiplexer_2_out, multiplexer_5_out,
       multiplexer_12_out;

  Clock clock_1 (.out(clock_1_out));
  or or_1 (or_1_out, FF1_qn, and_3_out, and_8_out, and_4_out);
  S_R_Flip_Flop FF1 (.S(FF1_qn), .clk(clock_1_out), .R(FF10_q), .Qn(FF1_qn));  // open: Q, preset, reset, en
  Counter #(.width(16), .max('hffff)) counter_1 (
    .load(FF10_q), .D(FR9_q), .count(or_1_out), .Q(counter_1_q), .clk(clock_1_out));  // open: carry, clr
  not not_1 (not_1_out, FF1_qn);
  Multiplexer #(.width(3), .enable("false")) multiplexer_1 (
    .in0(multiplexer_3_out), .in1(FR2_q[7:5]), .out(multiplexer_1_out), .sel(decoder_2_out2));
  Multiplexer #(.width(16), .enable("false")) multiplexer_2 (
    .in0(counter_1_q), .in1(adder_1_out), .out(multiplexer_2_out), .sel(or_2_out));
  or or_2 (or_2_out, and_7_out, and_11_out);
  S_R_Flip_Flop FF2 (.S(or_5_out), .clk(clock_1_out), .R(FF10_q), .Q(FF2_q), .Qn(FF2_qn));  // open: preset, reset, en
  or or_3 (or_3_out, FF2_qn, FF4_q);
  or or_4 (or_4_out, FF7_qn, FF6_q);
  and and_1 (and_1_out, or_3_out, FF5_q, FF9_qn, or_4_out);
  and and_2 (and_2_out, clock_1_out, not_5_out, and_11_out);
  Decoder #(.select(3), .disabled(0)) decoder_1 (
    .out0(decoder_1_out0), .out1(decoder_1_out1), .out2(decoder_1_out2), .out3(decoder_1_out3),
    .out4(decoder_1_out4), .out5(decoder_1_out5), .out6(decoder_1_out6), .out7(decoder_1_out7),
    .sel(multiplexer_1_out), .en(nor_1_out));
  assign controlled_buffer_1_out = not_2_out ? FR8_q : 8'bz;  // Controlled_Buffer controlled_buffer_1
  not not_2 (not_2_out, not_5_out);
  S_R_Flip_Flop FF3 (.S(and_3_out), .clk(clock_1_out), .R(FF10_q), .Qn(FF3_qn));  // open: Q, preset, reset, en
  not not_3 (not_3_out, and_8_out);
  and and_3 (and_3_out, FF2_q, not_1_out, FF3_qn, not_3_out);
  not not_4 (not_4_out, and_3_out);
  Register FR8 (.D(multiplexer_13_out), .en(and_1_out), .Q(FR8_q), .clk(clock_1_out));  // open: clr
  not not_5 (not_5_out, and_10_out);
  and and_4 (and_4_out, not_3_out, not_1_out, FF2_q, not_4_out, FF4_qn);
  Register ar (.D(FR8_q), .en(decoder_1_out0), .Q(ar_q), .clk(and_2_out));  // open: clr
  Register br (.D(FR8_q), .en(decoder_1_out1), .Q(br_q), .clk(and_2_out));  // open: clr
  Register cr (.D(FR8_q), .en(decoder_1_out2), .Q(cr_q), .clk(and_2_out));  // open: clr
  Register ur (.D(FR8_q), .en(decoder_1_out3), .Q(ur_q), .clk(and_2_out));  // open: clr
  Register sr (.D(FR8_q), .en(decoder_1_out4), .Q(sr_q), .clk(and_2_out));  // open: clr
  Register ir (.D(FR8_q), .en(decoder_1_out5), .Q(ir_q), .clk(and_2_out));  // open: clr
  Register jr (.D(FR8_q), .en(decoder_1_out6), .Q(jr_q), .clk(and_2_out));  // open: clr
  S_R_Flip_Flop light_flash (.S(decoder_1_out7), .Q(light_flash_q));  // open: clk, R, Qn, preset, reset, en
  RAM #(.addrWidth(16)) ram_1 (
    .addr(multiplexer_2_out), .data(controlled_buffer_1_out), .clk(clock_1_out), .ld(not_5_out));  // open: sel, clr
  S_R_Flip_Flop FF4 (.S(and_4_out), .clk(clock_1_out), .R(FF10_q), .Q(FF4_q), .Qn(FF4_qn));  // open: preset, reset, en
  and and_5 (and_5_out, light_flash_q, clock_2_out);
  Clock clock_2 (.out(clock_2_out));
  or or_5 (or_5_out, comparator_2_eq, and_9_out, or_8_out);
  S_R_Flip_Flop FF5 (.S(and_6_out), .clk(clock_1_out), .R(FF10_q), .Q(FF5_q), .Qn(FF5_qn));  // open: preset, reset, en
  and and_6 (and_6_out, not_1_out, or_6_out, FF5_qn);
  LED led_1 (.in(and_5_out));
  Register FR4 (.D(controlled_buffer_1_out), .en(and_4_out), .Q(FR4_q), .clk(clock_1_out));  // open: clr
  Register FR3 (.D(controlled_buffer_1_out), .en(and_3_out), .Q(FR3_q), .clk(clock_1_out));  // open: clr
  Register FR2 (.D(controlled_buffer_1_out), .en(and_8_out), .Q(FR2_q), .clk(clock_1_out), .clr(FF10_q));
  Register FR1 (.D(controlled_buffer_1_out), .en(FF1_qn), .Q(FR1_q), .clk(clock_1_out), .clr(FF10_q));
  S_R_Flip_Flop FF6 (.S(and_7_out), .clk(clock_1_out), .R(FF10_q), .Q(FF6_q), .Qn(FF6_qn));  // open: preset, reset, en
  not not_6 (not_6_out, and_4_out);
  Multiplexer #(.width(8), .enable("false")) multiplexer_3 (
    .in0(FR1_q), .in1(controlled_buffer_1_out), .out({multiplexer_3_out_2, multiplexer_3_out}), .sel(FF1_qn));
  and and_7 (and_7_out, FF6_qn, not_3_out, not_1_out, not_4_out, not_6_out, FF7_q);
  S_R_Flip_Flop FF7 (.S(or_7_out), .clk(clock_1_out), .R(FF10_q), .Q(FF7_q), .Qn(FF7_qn));  // open: preset, reset, en
  and and_8 (and_8_out, not_1_out, FF7_q, FF8_qn);
  or or_6 (or_6_out, FF8_q, FF7_qn);
  Multiplexer #(.select(3), .width(8), .enable("false")) multiplexer_4 (
    .in0(ar_q), .in1(br_q), .in2(cr_q), .in3(ur_q), .in4(sr_q), .in5(ir_q), .in6(jr_q),
    .in7(counter_1_q[7:0]), .out(multiplexer_4_out), .sel(multiplexer_3_out));
  Multiplexer #(.select(3), .width(8), .enable("false")) multiplexer_5 (
    .in0(ar_q), .in1(br_q), .in2(cr_q), .in3(ur_q), .in4(sr_q), .in5(ir_q), .in6(jr_q), .in7(FR3_q),
    .out(multiplexer_5_out[7:0]), .sel(FR2_q[7:5]));
  Multiplexer #(.select(3), .width(8), .enable("false")) multiplexer_6 (
    .in0(ar_q), .in1(br_q), .in2(cr_q), .in3(ur_q), .in4(sr_q), .in5(ir_q), .in6(jr_q),
    .in7(counter_1_q[15:8]), .out(multiplexer_6_out), .sel(FR2_q[4:2]));
  S_R_Flip_Flop FF8 (.S(and_8_out), .clk(clock_1_out), .R(FF10_q), .Q(FF8_q), .Qn(FF8_qn));  // open: preset, reset, en
  Comparator #(.width(3), .mode("unsigned")) comparator_1 (
    .a(3'b111), .b(controlled_buffer_1_out[7:5]), .eq(comparator_1_eq));  // open: gt, lt
  S_R_Flip_Flop FF9 (.S(and_1_out), .clk(clock_1_out), .R(FF10_q), .Q(FF9_q), .Qn(FF9_qn));  // open: preset, reset, en
  Register FR5 (.D(multiplexer_4_out), .en(and_6_out), .Q(FR5_q), .clk(clock_1_out));  // open: clr
  Register FR6 (.D(multiplexer_6_out), .en(and_6_out), .Q(FR6_q), .clk(clock_1_out));  // open: clr
  and and_9 (and_9_out, and_8_out, comparator_1_eq);
  and and_10 (and_10_out, decoder_2_out2, and_11_out);
  and and_11 (and_11_out, FF9_q, FF10_qn);
  Comparator #(.width(3), .mode("unsigned")) comparator_2 (
    .a(multiplexer_3_out), .b(3'b111), .eq(comparator_2_eq));  // open: gt, lt
  Adder #(.width(16)) adder_1 (
    .a(multiplexer_5_out), .b(bit_extender_2_out), .out(adder_1_out), .cout(adder_1_cout));  // open: cin
  assign bit_extender_1_out = {{7{1'b0}}, adder_1_cout};  // Bit_Extender bit_extender_1
  Pull_Resistor pull_resistor_1 (.node(adder_1_cout));
  Comparator #(.width(2), .mode("unsigned")) comparator_3 (
    .a(FR2_q[1:0]), .b(2'b00), .gt(comparator_3_gt));  // open: eq, lt
  S_R_Flip_Flop FF10 (
    .S(and_11_out), .clk(clock_1_out), .R(FF10_q), .Q(FF10_q), .Qn(FF10_qn));  // open: preset, reset, en
  Comparator #(.width(3), .mode("unsigned")) comparator_4 (
    .a(3'b111), .b(FR2_q[7:5]), .eq(comparator_4_eq));  // open: gt, lt
  Multiplexer #(.width(8), .enable("false")) multiplexer_7 (
    .in0(ur_q), .in1(FR4_q), .out(multiplexer_7_out), .sel(comparator_4_eq));
  Decoder #(.select(5), .disabled(0), .enable("false")) decoder_2 (
    .out0(decoder_2_out0), .out1(decoder_2_out1), .out2(decoder_2_out2), .out3(decoder_2_out3),
    .out4(decoder_2_out4), .out5(decoder_2_out5), .out6(decoder_2_out6), .out7(decoder_2_out7),
    .out8(decoder_2_out8), .out9(decoder_2_out9), .out10(decoder_2_out10), .out11(decoder_2_out11),
    .out12(decoder_2_out12), .out13(decoder_2_out13), .out14(decoder_2_out14), .out15(decoder_2_out15),
    .out16(decoder_2_out16), .out17(decoder_2_out17), .out18(decoder_2_out18), .out19(decoder_2_out19),
    .out20(decoder_2_out20), .out21(decoder_2_out21), .out22(decoder_2_out22), .out23(decoder_2_out23),
    .out24(decoder_2_out24), .out25(decoder_2_out25), .out26(decoder_2_out26), .out27(decoder_2_out27),
    .out28(decoder_2_out28), .out29(decoder_2_out29), .out30(decoder_2_out30), .out31(decoder_2_out31),
    .sel(multiplexer_3_out_2));
  not not_7 (not_7_out, FF1_qn);
  Comparator #(.width(2), .mode("unsigned")) comparator_5 (
    .a(FR2_q[1:0]), .b(2'b00), .gt(comparator_5_gt));  // open: eq, lt
  Register FR7 (.D(multiplexer_8_out), .en(and_7_out), .Q(FR7_q), .clk(clock_1_out));  // open: clr
  Adder adder_2 (.a(multiplexer_7_out), .b(bit_extender_1_out), .out(multiplexer_5_out[15:8]));  // open: cin, cout
  assign bit_extender_2_out = {{8{multiplexer_9_out[7]}}, multiplexer_9_out};  // Bit_Extender bit_extender_2
  or or_7 (or_7_out, decoder_2_out1, decoder_2_out2, decoder_2_out3, decoder_2_out4, decoder_2_out5, decoder_2_out6, decoder_2_out7, decoder_2_out10, decoder_2_out11);
  Multiplexer #(.width(8), .enable("false")) multiplexer_8 (
    .in0(multiplexer_5_out[7:0]), .in1(controlled_buffer_1_out), .out(multiplexer_8_out),
    .sel(comparator_5_gt));
  Multiplexer #(.select(2), .width(8), .enable("false")) multiplexer_9 (
    .in1({8{1'b0}}), .in2(ir_q), .in3(jr_q), .out(multiplexer_9_out), .sel(FR2_q[1:0]));  // open: in0
  not not_8 (not_8_out, Z_q);
  Multiplexer #(.select(5), .enable("false")) multiplexer_10 (
    .in12(1'b1), .in13(1'b1), .in14(Z_q), .in15(not_8_out), .in16(N_q), .in17(not_9_out), .in18(C_q),
    .in19(not_10_out), .out(multiplexer_10_out), .sel(multiplexer_3_out_2));  // open: in0, in1, in2, in3, in4, in5, in6, in7, in8, in9, in10, in11, in20, in21, in22, in23, in24, in25, in26, in27, in28, in29, in30, in31
  not not_9 (not_9_out, N_q);
  not not_10 (not_10_out, C_q);
  Pull_Resistor pull_resistor_2 (.node(multiplexer_10_out));
  Multiplexer #(.width(8), .enable("false")) multiplexer_11 (
    .in0(FR3_q), .in1(FR5_q), .out(multiplexer_11_out), .sel(decoder_2_out13));
  Multiplexer #(.width(16), .enable("false")) multiplexer_12 (
    .in0(counter_1_q), .in1({FR4_q, multiplexer_11_out}), .out(multiplexer_12_out), .sel(multiplexer_10_out));
  Register #(.width(16)) FR9 (.D(multiplexer_12_out), .en(and_1_out), .Q(FR9_q), .clk(clock_1_out));  // open: clr
  or or_8 (or_8_out, decoder_2_out12, decoder_2_out14, decoder_2_out15, decoder_2_out16, decoder_2_out17, decoder_2_out18, decoder_2_out19);
  nor nor_1 (nor_1_out, decoder_2_out0, or_8_out);
  assign and_12_out = FR7_q & FR6_q;  // AND_Gate and_12, 8 bits wide
  assign or_9_out = FR7_q | FR6_q;  // OR_Gate or_9, 8 bits wide
  and and_13 (and_13_out, adder_4_cout, decoder_2_out20);
  and and_14 (and_14_out, decoder_2_out21, subtractor_2_bout);
  and and_15 (and_15_out, decoder_2_out3, subtractor_1_bout);
  and and_16 (and_16_out, adder_3_cout, decoder_2_out4);
  and and_17 (and_17_out, and_1_out, nor_2_out);
  Adder adder_3 (.a(FR7_q), .b(FR6_q), .out(adder_3_out), .cout(adder_3_cout));  // open: cin
  Subtractor subtractor_1 (.a(FR7_q), .b(FR6_q), .out(subtractor_1_out), .bout(subtractor_1_bout));  // open: bin
  assign xor_1_out = FR7_q ^ FR6_q;  // XOR_Gate xor_1, 8 bits wide
  Shifter shifter_1 (.in(FR7_q), .\dist (FR6_q[2:0]), .out(shifter_1_out));
  Shifter #(.shift("lr")) shifter_2 (.in(FR7_q), .\dist (FR6_q[2:0]), .out(shifter_2_out));
  Adder adder_4 (.a(FR5_q), .b(8'h1), .out(adder_4_out), .cout(adder_4_cout));  // open: cin
  Subtractor subtractor_2 (.a(FR5_q), .b(8'h1), .out(subtractor_2_out), .bout(subtractor_2_bout));  // open: bin
  or or_10 (or_10_out, and_15_out, and_13_out, and_14_out, and_16_out);
  Comparator comparator_6 (
    .a({8{1'b0}}), .b(multiplexer_13_out), .eq(comparator_6_eq), .lt(comparator_6_lt));  // open: gt
  nor nor_2 (nor_2_out, decoder_2_out12, decoder_2_out13, decoder_2_out14, decoder_2_out15, decoder_2_out17, decoder_2_out18, decoder_2_out19);
  Negator negator_1 (.in(FR5_q), .out(negator_1_out));
  assign not_11_out = ~FR5_q;  // NOT_Gate not_11, 8 bits wide
  D_Flip_Flop C (.clk(clock_1_out), .D(or_10_out), .Q(C_q), .en(and_17_out));  // open: Qn, preset, reset
  D_Flip_Flop Z (.clk(clock_1_out), .D(comparator_6_eq), .Q(Z_q), .en(and_17_out));  // open: Qn, preset, reset
  D_Flip_Flop N (.clk(clock_1_out), .D(comparator_6_lt), .Q(N_q), .en(and_17_out));  // open: Qn, preset, reset
  Multiplexer #(.select(5), .width(8), .enable("false")) multiplexer_13 (
    .in1(FR7_q), .in2(FR6_q), .in3(adder_3_out), .in4(subtractor_1_out), .in5(and_12_out), .in6(or_9_out),
    .in7(xor_1_out), .in8(not_11_out), .in9(negator_1_out), .in10(shifter_1_out), .in11(shifter_2_out),
    .in20(adder_4_out), .in21(subtractor_2_out), .out(multiplexer_13_out), .sel(multiplexer_3_out_2));  // open: in0, in12, in13, in14, in15, in16, in17, in18, in19, in22, in23, in24, in25, in26, in27, in28, in29, in30, in31

  // Notes on the sheet:
  //   1.
  //   RousTel r1337
  //   circuit diagram
  //   This is proprietary information,
  //   make sure that nobody
  //   gets this diagram so that
  //   they can't rev my secret
  //   proprietary flag encryption
  //   algorithm!
  //   7.
  //   3.
  //   MAIN MEMORY
  //   PUT PROGRAM HERE
  //   4.
  //   5.
  //   6.
  //   2.
  //   8.
endmodule
